// Logisim project contador_senha.circ as structural Verilog: 1 circuit, main circuit main
module main (
  input  add,
  input  [2:0] s,
  output cont_end,
  output [1:0] Q
);

  wire and_1_out, clock, clr, D, d_ff_1_qn, d_ff_2_qn, demultiplexer_1_out0, or_1_out;

  Demultiplexer #(.select(3), .enable("false")) demultiplexer_1 (
    .out0(demultiplexer_1_out0), .out2(D), .in(add), .sel(s));  // open: out1, out3, out4, out5, out6, out7
  Clock clk (.out(clock));
  not not_1 (clr, demultiplexer_1_out0);
  D_Flip_Flop #(.NegatePresetClear("true")) d_ff_1 (
    .clk(clock), .D(Q[0]), .Q(Q[1]), .Qn(d_ff_1_qn), .preset(d_ff_1_qn), .reset(clr));
  Demultiplexer #(.select(2), .enable("false")) demultiplexer_2 (
    .out3(cont_end), .in(1'b1), .sel(Q));  // open: out0, out1, out2
  and and_1 (and_1_out, D, d_ff_2_qn);
  or or_1 (or_1_out, d_ff_1_qn, d_ff_2_qn);
  D_Flip_Flop #(.NegatePresetClear("true"), .enable("true")) d_ff_2 (
    .clk(clock), .D(and_1_out), .Q(Q[0]), .Qn(d_ff_2_qn), .en(or_1_out), .reset(clr));  // open: preset
endmodule
