// Logisim project led.circ as structural Verilog: 1 circuit, main circuit main
module main (
  input  [2:0] s,
  output LEDR,
  output LEDB,
  output LEDG
);

  wire demultiplexer_1_out0, demultiplexer_1_out1, demultiplexer_1_out2, demultiplexer_1_out3,
       demultiplexer_1_out4;

  Demultiplexer #(.select(3), .enable("false")) demultiplexer_1 (
    .out0(demultiplexer_1_out0), .out1(demultiplexer_1_out1), .out2(demultiplexer_1_out2),
    .out3(demultiplexer_1_out3), .out4(demultiplexer_1_out4), .out5(LEDG), .in(1'b1), .sel(s));  // open: out6, out7
  or or_1 (LEDR, demultiplexer_1_out0, demultiplexer_1_out2, demultiplexer_1_out4);
  or or_2 (LEDB, demultiplexer_1_out1, demultiplexer_1_out3);
endmodule
