// Logisim project timer.circ as structural Verilog: 1 circuit, main circuit main
module main (
  input  senha_ok,
  input  [2:0] s,
  output [4:0] Q,
  output tmr_5,
  output tmr_20,
  output tmr_25
);

  wire and_5_out, and_7_out, clk_out, clr, demultiplexer_1_out1, demultiplexer_1_out3, demultiplexer_1_out4,
       demultiplexer_1_out5, JK2, JK3, JK4, not_1_out, not_2_out, not_3_out, not_4_out, not_5_out, not_6_out,
       not_7_out, not_8_out, not_9_out;

  Clock clk (.out(clk_out));
  and and_1 (JK2, Q[0], Q[1]);
  Demultiplexer #(.select(3), .enable("false")) demultiplexer_1 (
    .out1(demultiplexer_1_out1), .out3(demultiplexer_1_out3), .out4(demultiplexer_1_out4),
    .out5(demultiplexer_1_out5), .in(1'b1), .sel(s));  // open: out0, out2, out6, out7
  J_K_Flip_Flop #(.NegatePresetClear("true")) j_k_ff_1 (
    .J(1'b1), .clk(clk_out), .K(1'b1), .Q(Q[0]), .preset(1'b1), .reset(clr));  // open: Qn
  and and_2 (JK3, Q[0], Q[1], Q[2]);
  J_K_Flip_Flop #(.NegatePresetClear("true")) j_k_ff_2 (
    .J(Q[0]), .clk(clk_out), .K(Q[0]), .Q(Q[1]), .preset(1'b1), .reset(clr));  // open: Qn
  not not_1 (not_1_out, Q[1]);
  not not_2 (not_2_out, Q[3]);
  not not_3 (not_3_out, Q[4]);
  or or_1 (clr, demultiplexer_1_out1, demultiplexer_1_out3, demultiplexer_1_out4, demultiplexer_1_out5);
  and and_3 (JK4, Q[0], Q[1], Q[2], Q[3]);
  J_K_Flip_Flop #(.NegatePresetClear("true")) j_k_ff_3 (
    .J(JK2), .clk(clk_out), .K(JK2), .Q(Q[2]), .preset(1'b1), .reset(clr));  // open: Qn
  and and_4 (tmr_5, Q[0], not_1_out, Q[2], not_2_out, not_3_out);
  J_K_Flip_Flop #(.NegatePresetClear("true")) j_k_ff_4 (
    .J(JK3), .clk(clk_out), .K(JK3), .Q(Q[3]), .preset(1'b1), .reset(clr));  // open: Qn
  J_K_Flip_Flop #(.NegatePresetClear("true")) j_k_ff_5 (
    .J(JK4), .clk(clk_out), .K(JK4), .Q(Q[4]), .preset(1'b1), .reset(clr));  // open: Qn
  not not_4 (not_4_out, Q[0]);
  not not_5 (not_5_out, Q[1]);
  not not_6 (not_6_out, Q[3]);
  not not_7 (not_7_out, Q[1]);
  not not_8 (not_8_out, Q[2]);
  and and_5 (and_5_out, not_4_out, not_5_out, Q[2], not_6_out, Q[4]);
  and and_6 (tmr_25, Q[0], not_7_out, not_8_out, Q[3], Q[4]);
  not not_9 (not_9_out, senha_ok);
  and and_7 (and_7_out, not_9_out, and_5_out);
  or or_2 (tmr_20, and_7_out, tmr_25);
endmodule
