// Logisim project contador_cres_decres.circ as structural Verilog: 1 circuit, main circuit main
module main (
  input  up_dw,
  input  clr,
  output [3:0] cont
);

  wire and_1_out, and_2_out, and_3_out, and_4_out, and_5_out, and_6_out, clock_out, JK_1, JK_2, JK_3,
       not_1_out, not_2_out, not_3_out, not_4_out, not_5_out, not_6_out, not_7_out, undriven;

  not not_1 (not_1_out, up_dw);
  Clock clock (.out(clock_out));
  and and_1 (and_1_out, up_dw, cont[0], cont[1], cont[2]);
  not not_2 (not_2_out, cont[0]);
  not not_3 (not_3_out, cont[1]);
  and and_2 (and_2_out, not_2_out, not_3_out, not_4_out, not_1_out);
  not not_4 (not_4_out, cont[2]);
  or or_1 (JK_3, and_1_out, and_2_out);
  not not_5 (not_5_out, cont[0]);
  not not_6 (not_6_out, cont[1]);
  J_K_Flip_Flop #(.NegatePresetClear("true")) j_k_ff_1 (
    .J(1'b1), .clk(clock_out), .K(1'b1), .Q(cont[0]), .preset(1'b1), .reset(clr));  // open: Qn
  and and_3 (and_3_out, up_dw, cont[0], cont[1]);
  or or_2 (JK_2, and_3_out, and_4_out);
  and and_4 (and_4_out, not_5_out, not_6_out, not_1_out);
  and and_5 (and_5_out, up_dw, cont[0]);
  not not_7 (not_7_out, cont[0]);
  and and_6 (and_6_out, not_7_out, not_1_out);
  J_K_Flip_Flop #(.NegatePresetClear("true")) j_k_ff_2 (
    .J(JK_1), .clk(clock_out), .K(JK_1), .Q(cont[1]), .preset(1'b1), .reset(clr));  // open: Qn
  or or_3 (JK_1, and_5_out, and_6_out);
  J_K_Flip_Flop #(.NegatePresetClear("true")) j_k_ff_3 (
    .J(JK_2), .clk(clock_out), .K(JK_2), .Q(cont[2]), .preset(1'b1), .reset(clr));  // open: Qn
  J_K_Flip_Flop #(.NegatePresetClear("true")) j_k_ff_4 (
    .J(JK_3), .clk(clock_out), .K(JK_3), .Q(cont[3]), .preset(undriven), .reset(clr));  // open: Qn

  // Other names for the same wires on the sheet: Q_0 = cont[0]; Q_1 = cont[1]; Q_2 = cont[2]; Q_3 = cont[3]
endmodule
