// Logisim project regi_max.circ as structural Verilog: 1 circuit, main circuit main
module main (
  input  [11:0] in_1,
  input  load,
  input  mx_mi,
  input  clr,
  output [11:0] out_5
);

  wire clk, en_mx, undriven, undriven_2;

  Clock clock_1 (.out(clk));
  and and_1 (en_mx, load, mx_mi);
  D_Flip_Flop #(.NegatePresetClear("true"), .enable("true")) d_ff_1 (
    .clk(clk), .D(in_1[11]), .Q(out_5[11]), .preset(clr), .en(en_mx), .reset(undriven));  // open: Qn
  D_Flip_Flop #(.NegatePresetClear("true"), .enable("true")) d_ff_2 (
    .clk(clk), .D(in_1[10]), .Q(out_5[10]), .en(en_mx), .reset(clr));  // open: Qn, preset
  D_Flip_Flop #(.NegatePresetClear("true"), .enable("true")) d_ff_3 (
    .clk(clk), .D(in_1[9]), .Q(out_5[9]), .en(en_mx), .reset(clr));  // open: Qn, preset
  D_Flip_Flop #(.NegatePresetClear("true"), .enable("true")) d_ff_4 (
    .clk(clk), .D(in_1[8]), .Q(out_5[8]), .preset(clr), .en(en_mx));  // open: Qn, reset
  D_Flip_Flop #(.NegatePresetClear("true"), .enable("true")) d_ff_5 (
    .clk(clk), .D(in_1[7]), .Q(out_5[7]), .preset(clr), .en(en_mx), .reset(undriven_2));  // open: Qn
  D_Flip_Flop #(.NegatePresetClear("true"), .enable("true")) d_ff_6 (
    .clk(clk), .D(in_1[6]), .Q(out_5[6]), .en(en_mx), .reset(clr));  // open: Qn, preset
  D_Flip_Flop #(.NegatePresetClear("true"), .enable("true")) d_ff_7 (
    .clk(clk), .D(in_1[5]), .Q(out_5[5]), .en(en_mx), .reset(clr));  // open: Qn, preset
  D_Flip_Flop #(.NegatePresetClear("true"), .enable("true")) d_ff_8 (
    .clk(clk), .D(in_1[4]), .Q(out_5[4]), .preset(clr), .en(en_mx));  // open: Qn, reset
  D_Flip_Flop #(.NegatePresetClear("true"), .enable("true")) d_ff_9 (
    .clk(clk), .D(in_1[3]), .Q(out_5[3]), .preset(clr), .en(en_mx));  // open: Qn, reset
  D_Flip_Flop #(.NegatePresetClear("true"), .enable("true")) d_ff_10 (
    .clk(clk), .D(in_1[2]), .Q(out_5[2]), .en(en_mx), .reset(clr));  // open: Qn, preset
  D_Flip_Flop #(.NegatePresetClear("true"), .enable("true")) d_ff_11 (
    .clk(clk), .D(in_1[1]), .Q(out_5[1]), .en(en_mx), .reset(clr));  // open: Qn, preset
  D_Flip_Flop #(.NegatePresetClear("true"), .enable("true")) d_ff_12 (
    .clk(clk), .D(in_1[0]), .Q(out_5[0]), .preset(clr), .en(en_mx));  // open: Qn, reset
endmodule
