// Logisim project regi_passo.circ as structural Verilog: 1 circuit, main circuit main
module main (
  input  [3:0] in_1,
  input  load,
  input  step,
  input  clr,
  output [3:0] out_5
);

  wire clk, en_stp;

  Clock clock_1 (.out(clk));
  and and_1 (en_stp, load, step);
  D_Flip_Flop #(.NegatePresetClear("true"), .enable("true")) d_ff_1 (
    .clk(clk), .D(in_1[3]), .Q(out_5[3]), .en(en_stp), .reset(clr));  // open: Qn, preset
  D_Flip_Flop #(.NegatePresetClear("true"), .enable("true")) d_ff_2 (
    .clk(clk), .D(in_1[2]), .Q(out_5[2]), .en(en_stp), .reset(clr));  // open: Qn, preset
  D_Flip_Flop #(.NegatePresetClear("true"), .enable("true")) d_ff_3 (
    .clk(clk), .D(in_1[1]), .Q(out_5[1]), .en(en_stp), .reset(clr));  // open: Qn, preset
  D_Flip_Flop #(.NegatePresetClear("true"), .enable("true")) d_ff_4 (
    .clk(clk), .D(in_1[0]), .Q(out_5[0]), .preset(clr), .en(en_stp));  // open: Qn, reset
endmodule
