// Logisim project saida_L.circ as structural Verilog: 1 circuit, main circuit main
module main (
  input  [1:0] s,
  input  clr,
  output L
);

  wire clk_out, decoder_1_out1, decoder_1_out2, decoder_1_out3, j_k_ff_1_q;

  Clock clk (.out(clk_out));
  Decoder #(.select(2), .enable("false")) decoder_1 (
    .out1(decoder_1_out1), .out2(decoder_1_out2), .out3(decoder_1_out3), .sel(s));  // open: out0
  J_K_Flip_Flop #(.NegatePresetClear("true")) j_k_ff_1 (
    .J(decoder_1_out3), .clk(clk_out), .K(decoder_1_out3), .Q(j_k_ff_1_q), .reset(clr));  // open: Qn, preset
  or or_1 (L, decoder_1_out1, decoder_1_out2, j_k_ff_1_q);
endmodule
