// Logisim project timer40.circ as structural Verilog: 1 circuit, main circuit main
module main (
  output [5:0] Q,
  output tmr_40,
  output tmr_10
);

  wire and_3_out, clk_out, clr, JK2, JK3, JK4, JK5, not_1_out, not_2_out, not_3_out, not_5_out, not_6_out,
       not_7_out, not_8_out, not_9_out, not_10_out, not_11_out, not_12_out;

  Clock clk (.out(clk_out));
  and and_1 (JK2, Q[0], Q[1]);
  not not_1 (not_1_out, Q[1]);
  not not_2 (not_2_out, Q[2]);
  not not_3 (not_3_out, Q[4]);
  J_K_Flip_Flop #(.NegatePresetClear("true")) j_k_ff_1 (
    .J(1'b1), .clk(clk_out), .K(1'b1), .Q(Q[0]), .preset(1'b1), .reset(clr));  // open: Qn
  and and_2 (JK3, Q[0], Q[1], Q[2]);
  and and_3 (and_3_out, Q[0], not_1_out, not_2_out, Q[3], not_3_out, Q[5]);
  J_K_Flip_Flop #(.NegatePresetClear("true")) j_k_ff_2 (
    .J(Q[0]), .clk(clk_out), .K(Q[0]), .Q(Q[1]), .preset(1'b1), .reset(clr));  // open: Qn
  not not_4 (clr, and_3_out);
  and and_4 (JK4, Q[0], Q[1], Q[2], Q[3]);
  J_K_Flip_Flop #(.NegatePresetClear("true")) j_k_ff_3 (
    .J(JK2), .clk(clk_out), .K(JK2), .Q(Q[2]), .preset(1'b1), .reset(clr));  // open: Qn
  not not_5 (not_5_out, Q[0]);
  not not_6 (not_6_out, Q[1]);
  not not_7 (not_7_out, Q[2]);
  not not_8 (not_8_out, Q[4]);
  J_K_Flip_Flop #(.NegatePresetClear("true")) j_k_ff_4 (
    .J(JK3), .clk(clk_out), .K(JK3), .Q(Q[3]), .preset(1'b1), .reset(clr));  // open: Qn
  J_K_Flip_Flop #(.NegatePresetClear("true")) j_k_ff_5 (
    .J(JK4), .clk(clk_out), .K(JK4), .Q(Q[4]), .preset(1'b1), .reset(clr));  // open: Qn
  and and_5 (tmr_40, not_5_out, not_6_out, not_7_out, Q[3], not_8_out, Q[5]);
  and and_6 (JK5, Q[0], Q[1], Q[2], Q[3], Q[4]);
  J_K_Flip_Flop #(.NegatePresetClear("true")) j_k_ff_6 (
    .J(JK5), .clk(clk_out), .K(JK5), .Q(Q[5]), .preset(1'b1), .reset(clr));  // open: Qn
  not not_9 (not_9_out, Q[0]);
  not not_10 (not_10_out, Q[2]);
  not not_11 (not_11_out, Q[4]);
  not not_12 (not_12_out, Q[5]);
  and and_7 (tmr_10, not_9_out, Q[1], not_10_out, Q[3], not_11_out, not_12_out);
endmodule
